# Fritzing sketch esquematico (saved by Fritzing 1.0.1rc)

parts:
  MFS1 = Multi Function Shield
  DS1 = DS18B20 1-Wire Temperature Sensor [part_number=DS18B20]

nets:
  GND: MFS1.GND, DS1.GND
  N1: MFS1.J1-A4, DS1.DQ
  VCC: MFS1.VCC, DS1.VDD

custom parts:
  Multi Function Shield: Das Multi Function Shield kann auf den Arduino Uno aufgesteckt werden und bietet ein paar wichtige Bauteile.
